// Logisim project homework.circ as structural Verilog: 5 circuits, main circuit P5_Popcount13
module P1_Logic4 (
  input  a,
  input  b,
  input  c,
  input  d,
  output out1,
  output out2
);

  or or_1 (out2, a, b, c, d);
  and and_1 (out1, a, b, c, d);
endmodule

module P2_Mux8 (
  input  [7:0] din,
  input  [2:0] sel,
  output y
);

  Multiplexer #(.select(3)) multiplexer_1 (
    .in0(din[0]), .in1(din[1]), .in2(din[2]), .in3(din[3]), .in4(din[4]), .in5(din[5]), .in6(din[6]),
    .in7(din[7]), .out(y), .sel(sel));

  // Notes on the sheet:
  //   2. 8-to-1 MUX: sel=0 selects din[0]
endmodule

module P3_Letters (
  input  [2:0] code,
  output [6:0] seg
);

  ROM #(.addrWidth(3), .dataWidth(7)) rom_1 (.addr(code), .data(seg));
  _7_Segment_Display u_7_segment_display_1 (
    .g(seg[0]), .f(seg[1]), .a(seg[6]), .b(seg[5]), .e(seg[2]), .d(seg[3]), .c(seg[4]), .dp(1'b0));

  // Other names for the same wires on the sheet: s0 = seg[0]; s1 = seg[1]; s2 = seg[2]; s3 = seg[3]; s4 = seg[4];
  //   s5 = seg[5]; s6 = seg[6]

  // Notes on the sheet:
  //   contents of rom_1 (hex, n*v repeats v):
  //   7d 1f d 3d 47 7b
endmodule

module P4_Vote25 (
  input  [24:0] vt,
  output [4:0] count,
  output result
);

  BitAdder #(.width(25)) bitadder_1 (.in0(vt), .out(count));
  Comparator #(.mode("unsigned"), .width(5)) comparator_1 (.a(count), .b(5'b01100), .gt(result));  // open: eq, lt
endmodule

module P5_Popcount13 (
  input  [12:0] vt,
  input  en,
  output [3:0] count,
  output [6:0] seg
);

  wire [6:0] MASK, RAW;

  ROM #(.addrWidth(4), .dataWidth(7)) rom_1 (.addr(count), .data(RAW));
  BitAdder #(.width(13)) bitadder_1 (.in0(vt), .out(count));
  assign MASK = {{6{en}}, en};  // Bit_Extender bit_extender_1
  assign seg = RAW & MASK;  // AND_Gate and_1, 7 bits wide
  _7_Segment_Display u_7_segment_display_1 (
    .g(seg[0]), .f(seg[1]), .a(seg[6]), .b(seg[5]), .e(seg[2]), .d(seg[3]), .c(seg[4]), .dp(1'b0));

  // Other names for the same wires on the sheet: s0 = seg[0]; s1 = seg[1]; s2 = seg[2]; s3 = seg[3]; s4 = seg[4];
  //   s5 = seg[5]; s6 = seg[6]

  // Notes on the sheet:
  //   contents of rom_1 (hex, n*v repeats v):
  //   7e 30 6d 79 33 5b 5f 70 7f 7b 77 1f 4e 3d 4f 47
endmodule
